# Fritzing sketch soil sensor (saved by Fritzing 0.9.5d)

parts:
  Mod1 = Raspberry Pi 4B  # not connected
  RS485_module1 = RS485 Module (MAX3485)
  JACK1 = 2.1mm Barrel Jack with Terminal Block
  A1 = JXBS-3001-NPK-RS smaller

nets:
  N1: RS485_module1.A, A1.Pin_3
  N2: RS485_module1.B, A1.Pin_4
  N3: JACK1.POS, A1.Pin_1
  N4: JACK1.NEG, A1.Pin_2

custom parts:
  RS485 Module (MAX3485): Commercially available RS485 to RS232 TTL Module
  JXBS-3001-NPK-RS smaller: The NPK sensor is designed for detecting the content of nitrogen, phosphorus and potassium in soil, determining the fertility of the soil and facilitating the evaluation of the soil condition by the customer system. This version has breadboard reduced in size to more closely match the 485 adapter and CPU board.
